// Digital circuit hw3_1.dig as structural Verilog
module hw3_1 (
  input  S0,
  input  S1,
  input  S2,
  output d0,
  output d1,
  output d2,
  output d3,
  output d4,
  output d5,
  output d6,
  output d7
);

  wire not_1_out;

  not not_1 (not_1_out, S2);
  Demultiplexer #(.Selector_Bits(2)) demultiplexer_1 (
    .sel({S1, S0}), .in(not_1_out), .out_0(d0), .out_1(d1), .out_2(d2), .out_3(d3));
  Demultiplexer #(.Selector_Bits(2)) demultiplexer_2 (
    .sel({S1, S0}), .in(S2), .out_0(d4), .out_1(d5), .out_2(d6), .out_3(d7));
endmodule
