// Digital circuit hw3_2.dig as structural Verilog
module hw3_2 (
  input  S0,
  input  S1,
  input  S2,
  input  I0,
  input  I1,
  input  I2,
  input  I3,
  input  I4,
  input  I5,
  input  I6,
  input  I7,
  output d0
);

  wire multiplexer_1_out, multiplexer_2_out, multiplexer_3_out, multiplexer_4_out, multiplexer_5_out,
       multiplexer_6_out;

  Multiplexer multiplexer_1 (.sel(S0), .in_0(I0), .in_1(I1), .out(multiplexer_1_out));
  Multiplexer multiplexer_2 (.sel(S0), .in_0(I2), .in_1(I3), .out(multiplexer_2_out));
  Multiplexer multiplexer_3 (.sel(S0), .in_0(I4), .in_1(I5), .out(multiplexer_3_out));
  Multiplexer multiplexer_4 (.sel(S0), .in_0(I6), .in_1(I7), .out(multiplexer_4_out));
  Multiplexer multiplexer_5 (.sel(S1), .in_0(multiplexer_1_out), .in_1(multiplexer_2_out), .out(multiplexer_5_out));
  Multiplexer multiplexer_6 (.sel(S1), .in_0(multiplexer_3_out), .in_1(multiplexer_4_out), .out(multiplexer_6_out));
  Multiplexer multiplexer_7 (.sel(S2), .in_0(multiplexer_5_out), .in_1(multiplexer_6_out), .out(d0));
endmodule
