// Digital circuit hw3_3.dig as structural Verilog
module hw3_3 (
  input  x,
  input  y,
  input  z,
  output d0
);

  wire decoder_1_out_2, decoder_1_out_3, decoder_1_out_6, or_1_out;

  Decoder #(.Selector_Bits(3)) decoder_1 (
    .sel({z, y, x}), .out_2(decoder_1_out_2), .out_3(decoder_1_out_3), .out_6(decoder_1_out_6));  // open: out_0, out_1, out_4, out_5, out_7
  or or_1 (or_1_out, decoder_1_out_2, decoder_1_out_3);
  nor nor_1 (d0, or_1_out, decoder_1_out_6);
endmodule
