// Digital circuit hw3_4.dig as structural Verilog
module hw3_4 (
  input  z,
  input  y,
  input  x,
  output C,
  output S
);

  wire not_1_out;

  not not_1 (not_1_out, z);
  Multiplexer #(.Selector_Bits(2)) multiplexer_1 (.sel({x, y}), .in_0(1'b0), .in_1(z), .in_2(z), .in_3(1'b1), .out(C));
  Multiplexer #(.Selector_Bits(2)) multiplexer_2 (
    .sel({x, y}), .in_0(z), .in_1(not_1_out), .in_2(not_1_out), .in_3(z), .out(S));
endmodule
