// Digital circuit hw3_decoder_template.dig as structural Verilog
module hw3_decoder_template (
  input  S0,
  input  S1,
  output d0,
  output d1,
  output d2,
  output d3
);

  Decoder #(.Selector_Bits(2)) decoder_1 (.sel({S1, S0}), .out_0(d0), .out_1(d1), .out_2(d2), .out_3(d3));
endmodule
