// Digital circuit statemachine.dig as structural Verilog
module statemachine (
  input  A,
  input  B,
  input  CLK,
  output OUT
);

  wire and_1_out, and_2_out, and_3_out, and_4_out, and_5_out, not_1_out, not_2_out, not_3_out, not_4_out,
       or_1_out, or_2_out, Q_0_n, Q_1_n;

  not not_1 (not_1_out, A);
  not not_2 (not_2_out, B);
  not not_3 (not_3_out, Q_1_n);
  not not_4 (not_4_out, Q_0_n);
  and and_1 (and_1_out, A, B, Q_0_n, not_3_out);
  and and_2 (and_2_out, A, not_4_out, Q_1_n);
  and and_3 (and_3_out, A, not_2_out, Q_1_n);
  and and_4 (and_4_out, not_1_out, not_4_out, not_3_out);
  and and_5 (and_5_out, A, not_2_out, Q_1_n);
  and and_6 (OUT, not_1_out, not_2_out, Q_0_n, Q_1_n);
  or or_1 (or_1_out, and_1_out, and_2_out, and_3_out);
  or or_2 (or_2_out, and_4_out, and_5_out);
  D_FF u_Q_1_n (.D(or_1_out), .C(CLK), .Q(Q_1_n));  // open: nQ
  D_FF u_Q_0_n (.D(or_2_out), .C(CLK), .Q(Q_0_n));  // open: nQ
endmodule
