// Digital circuit counter.dig as structural Verilog
module counter (
  input  _100_Hz,
  input  RESET
);

  wire and_1_out, and_2_out, BD_out, BU_out, cntdecud_2_p6, cntdecud_2_p7;
  wire [3:0] cntdecud_1_p5, cntdecud_2_p5;

  and and_1 (and_1_out, cntdecud_2_p6, BD_out);
  and and_2 (and_2_out, cntdecud_2_p7, BU_out);
  // cntDECud cntdecud_1: pin names not known; wires that end beside it: and_2_out, and_1_out, _100_Hz, RESET, cntdecud_1_p5
  Button BU (.out(BU_out));
  Button BD (.out(BD_out));
  // cntDECud cntdecud_2: pin names not known; wires that end beside it: BU_out, BD_out, _100_Hz, RESET, cntdecud_2_p5, cntdecud_2_p6, cntdecud_2_p7
  Seven_Seg_Hex seven_seg_hex_1 (.d(cntdecud_1_p5), .dp(1'b0));
  Seven_Seg_Hex seven_seg_hex_2 (.d(cntdecud_2_p5), .dp(1'b0));

  // Notes on the sheet:
  //   _100_Hz: Hz: 100
endmodule
