// Digital circuit adder.dig as structural Verilog
module adder (
);

  wire dipswitch_7_out;
  wire [2:0] add_1_s, dipswitch_1_out, dipswitch_4_out;
  wire [3:3] add_1_c_o;

  DipSwitch dipswitch_1 (.out(dipswitch_1_out[2]));
  DipSwitch dipswitch_2 (.out(dipswitch_1_out[1]));
  DipSwitch dipswitch_3 (.out(dipswitch_1_out[0]));
  DipSwitch dipswitch_4 (.out(dipswitch_4_out[2]));
  DipSwitch dipswitch_5 (.out(dipswitch_4_out[1]));
  DipSwitch dipswitch_6 (.out(dipswitch_4_out[0]));
  DipSwitch dipswitch_7 (.out(dipswitch_7_out));
  Add #(.Bits(3)) add_1 (
    .a(dipswitch_1_out), .b(dipswitch_4_out), .c_i(dipswitch_7_out), .s(add_1_s), .c_o(add_1_c_o[3]));
  Seven_Seg_Hex seven_seg_hex_1 (.d({add_1_c_o[3], add_1_s}), .dp(1'b0));
endmodule
