// Digital circuit bin_to_gray.dig as structural Verilog
module bin_to_gray (
  input  MSB__A,
  input  B,
  input  C,
  input  LSB__D
);

  wire not_1_out, not_2_out, not_3_out, not_4_out;

  not not_1 (not_1_out, MSB__A);
  not not_2 (not_2_out, B);
  not not_3 (not_3_out, C);
  not not_4 (not_4_out, LSB__D);
  LED X__MSB ();  // open: in
  LED Y ();  // open: in
  LED Z ();  // open: in
  LED T__LSB ();  // open: in
endmodule
