// Digital circuit bin_to_gray.dig as structural Verilog
module bin_to_gray (
  input  MSB__A,
  input  B,
  input  C,
  input  LSB__D
);

  wire and_1_out, and_2_out, and_3_out, not_1_out, not_2_out, not_3_out, not_4_out, not_5_out, not_6_out,
       or_1_out, or_2_out, or_3_out, or_4_out, or_5_out, or_6_out;

  and and_1 (and_1_out, MSB__A, B);
  or or_1 (or_1_out, MSB__A, B);
  and and_2 (and_2_out, B, C);
  or or_2 (or_2_out, C, B);
  and and_3 (and_3_out, C, LSB__D);
  or or_3 (or_3_out, C, LSB__D);
  not not_1 (not_1_out, or_1_out);
  not not_2 (not_2_out, or_2_out);
  not not_3 (not_3_out, or_3_out);
  or or_4 (or_4_out, and_1_out, not_1_out);
  or or_5 (or_5_out, and_2_out, not_2_out);
  or or_6 (or_6_out, and_3_out, not_3_out);
  not not_4 (not_4_out, or_4_out);
  not not_5 (not_5_out, or_5_out);
  not not_6 (not_6_out, or_6_out);
  LED X__MSB (.in(MSB__A));
  LED Y (.in(not_4_out));
  LED Z (.in(not_5_out));
  LED T__LSB (.in(not_6_out));
endmodule
