// Digital circuit counter4test.dig as structural Verilog
module counter4test (
  input  clk
);

  wire [3:0] cnt4_1_p2;

  // cnt4 cnt4_1: pin names not known; wires that end beside it: clk, cnt4_1_p2
  Seven_Seg_Hex seven_seg_hex_1 (.d(cnt4_1_p2), .dp(1'b0));
endmodule
