// Digital circuit counter.dig as structural Verilog
module counter (
  input  _100_Hz,
  input  RESET
);

  wire and_1_out, and_2_out, and_3_out, and_4_out, and_5_out, and_6_out, and_7_out, and_8_out, and_9_out,
       and_10_out, and_11_out, and_12_out, and_13_out, and_14_out, BD_out, BU_out, cntdecud_2_p6,
       cntdecud_2_p7, d_ff_1_q, d_ff_2_q, d_ff_3_q, d_ff_4_q, not_1_out, not_2_out, not_3_out, not_4_out,
       or_1_out, or_2_out, or_3_out, or_4_out, or_5_out, or_6_out;
  wire [3:0] cntdecud_1_p5, cntdecud_2_p5;

  Button BU (.out(BU_out));
  Button BD (.out(BD_out));
  not not_1 (not_1_out, d_ff_1_q);
  not not_2 (not_2_out, d_ff_2_q);
  and and_1 (and_1_out, BD_out, d_ff_1_q);
  and and_2 (and_2_out, d_ff_2_q, not_1_out);
  and and_3 (and_3_out, BD_out, not_2_out, not_1_out);
  and and_4 (and_4_out, BD_out, d_ff_2_q, d_ff_1_q);
  and and_5 (and_5_out, BD_out, not_1_out);
  and and_6 (and_6_out, d_ff_2_q, not_1_out);
  or or_1 (or_1_out, and_1_out, and_2_out);
  or or_2 (or_2_out, and_3_out, and_4_out);
  or or_3 (or_3_out, and_5_out, and_6_out);
  D_FF d_ff_1 (.D(or_1_out), .C(_100_Hz), .Q(d_ff_1_q));  // open: nQ
  D_FF d_ff_2 (.D(or_2_out), .C(_100_Hz), .Q(d_ff_2_q));  // open: nQ
  not not_3 (not_3_out, d_ff_3_q);
  not not_4 (not_4_out, d_ff_4_q);
  and and_7 (and_7_out, BU_out, d_ff_3_q);
  and and_8 (and_8_out, d_ff_4_q, not_3_out);
  and and_9 (and_9_out, BU_out, not_4_out, not_3_out);
  and and_10 (and_10_out, BU_out, d_ff_4_q, d_ff_3_q);
  and and_11 (and_11_out, BU_out, not_3_out);
  and and_12 (and_12_out, d_ff_4_q, not_3_out);
  and and_13 (and_13_out, cntdecud_2_p6, or_3_out);
  or or_4 (or_4_out, and_7_out, and_8_out);
  or or_5 (or_5_out, and_9_out, and_10_out);
  or or_6 (or_6_out, and_11_out, and_12_out);
  and and_14 (and_14_out, cntdecud_2_p7, or_6_out);
  // cntDECud cntdecud_1: pin names not known; wires that end beside it: and_14_out, and_13_out, _100_Hz, RESET, cntdecud_1_p5
  D_FF d_ff_3 (.D(or_4_out), .C(_100_Hz), .Q(d_ff_3_q));  // open: nQ
  D_FF d_ff_4 (.D(or_5_out), .C(_100_Hz), .Q(d_ff_4_q));  // open: nQ
  // cntDECud cntdecud_2: pin names not known; wires that end beside it: or_6_out, or_3_out, _100_Hz, RESET, cntdecud_2_p5, cntdecud_2_p6, cntdecud_2_p7
  Seven_Seg_Hex seven_seg_hex_1 (.d(cntdecud_1_p5), .dp(1'b0));
  Seven_Seg_Hex seven_seg_hex_2 (.d(cntdecud_2_p5), .dp(1'b0));

  // Notes on the sheet:
  //   _100_Hz: Hz: 100
endmodule
