// Digital circuit abs.dig as structural Verilog
module abs (
  input  [5:0] in,
  output sign,
  output [5:0] out
);

  wire [5:0] neg_1_out;

  Neg #(.Bits(6)) neg_1 (.in(in), .out(neg_1_out));
  Multiplexer #(.Bits(6)) multiplexer_1 (.sel(in[5]), .in_0(in), .in_1(neg_1_out), .out(out));

  assign sign = in[5];
endmodule
