// Digital circuit lab1d.dig as structural Verilog
module lab1d (
  input  in_1,
  input  in_2,
  input  in_3,
  input  in_4,
  input  in_5,
  input  in_6,
  input  in_7,
  input  in_8
);

  wire [3:0] unsignedbcd7_1_tens, unsignedbcd7_1_units, unsignedbcd_1_tens, unsignedbcd_1_units,
       unsignedbcd_2_tens, unsignedbcd_2_units;
  wire [5:0] add_1_s;
  wire [6:6] add_1_c_o;

  Seven_Seg_Hex seven_seg_hex_1 (.d(unsignedbcd_1_tens), .dp(1'b0));
  Seven_Seg_Hex seven_seg_hex_2 (.d(unsignedbcd_1_units), .dp(1'b0));
  unsignedBCD unsignedbcd_1 (.Input({in_5, in_6, in_7, in_8}), .tens(unsignedbcd_1_tens), .units(unsignedbcd_1_units));
  Seven_Seg_Hex seven_seg_hex_3 (.d(unsignedbcd_2_tens), .dp(1'b0));
  Seven_Seg_Hex seven_seg_hex_4 (.d(unsignedbcd_2_units), .dp(1'b0));
  unsignedBCD unsignedbcd_2 (.Input({in_1, in_2, in_3, in_4}), .tens(unsignedbcd_2_tens), .units(unsignedbcd_2_units));
  Seven_Seg_Hex seven_seg_hex_5 (.d(unsignedbcd7_1_tens), .dp(1'b0));
  Seven_Seg_Hex seven_seg_hex_6 (.d(unsignedbcd7_1_units), .dp(1'b0));
  unsignedBCD7 unsignedbcd7_1 (
    .Input({add_1_c_o[6], add_1_s}), .tens(unsignedbcd7_1_tens), .units(unsignedbcd7_1_units));
  Add #(.Bits(6)) add_1 (
    .a({2'b00, in_1, in_2, in_3, in_4}), .b({in_5, in_6, in_7, in_8, 2'b00}), .c_i(1'b0), .s(add_1_s),
    .c_o(add_1_c_o[6]));

  // Notes on the sheet:
  //   4x
  //   +
  //   =
endmodule
