// Digital circuit bin_to_Petherick.dig as structural Verilog
module bin_to_Petherick (
  input  MSB__A,
  input  B,
  input  C,
  input  LSB__D
);

  wire and_1_out, and_2_out, and_3_out, and_4_out, and_5_out, and_6_out, and_7_out, and_8_out, and_9_out,
       and_10_out, and_11_out, and_12_out, and_13_out, and_14_out, and_15_out, and_16_out, and_17_out,
       not_1_out, not_2_out, not_3_out, not_4_out, not_5_out, not_6_out, not_7_out, or_1_out, or_2_out,
       or_3_out, or_4_out;

  not not_1 (not_1_out, MSB__A);
  not not_2 (not_2_out, B);
  not not_3 (not_3_out, C);
  not not_4 (not_4_out, LSB__D);
  and and_1 (and_1_out, LSB__D, C, not_2_out, not_1_out);
  and and_2 (and_2_out, not_4_out, not_3_out, B, not_1_out);
  and and_3 (and_3_out, LSB__D, not_3_out, B, not_1_out);
  and and_4 (and_4_out, not_4_out, C, B, not_1_out);
  and and_5 (and_5_out, not_4_out, not_3_out, not_2_out, not_1_out);
  and and_6 (and_6_out, LSB__D, not_3_out, not_2_out, not_1_out);
  and and_7 (and_7_out, not_4_out, not_3_out, not_2_out, MSB__A);
  and and_8 (and_8_out, LSB__D, not_3_out, not_2_out, MSB__A);
  and and_9 (and_9_out, not_4_out, not_3_out, not_2_out, not_1_out);
  and and_10 (and_10_out, not_4_out, not_3_out, B, not_1_out);
  and and_11 (and_11_out, LSB__D, not_3_out, B, not_1_out);
  and and_12 (and_12_out, LSB__D, not_3_out, not_2_out, MSB__A);
  and and_13 (and_13_out, not_4_out, not_3_out, not_2_out, not_1_out);
  and and_14 (and_14_out, LSB__D, not_3_out, not_2_out, not_1_out);
  and and_15 (and_15_out, not_4_out, C, not_2_out, not_1_out);
  and and_16 (and_16_out, LSB__D, C, not_2_out, not_1_out);
  and and_17 (and_17_out, not_4_out, not_3_out, B, not_1_out);
  or or_1 (or_1_out, and_1_out, and_2_out, and_3_out, and_4_out);
  or or_2 (or_2_out, and_5_out, and_6_out, and_7_out, and_8_out);
  or or_3 (or_3_out, and_9_out, and_10_out, and_11_out, and_12_out);
  or or_4 (or_4_out, and_13_out, and_14_out, and_15_out, and_16_out, and_17_out);
  not not_5 (not_5_out, or_1_out);
  not not_6 (not_6_out, or_2_out);
  not not_7 (not_7_out, or_4_out);
  LED X__MSB (.in(not_5_out));
  LED Y (.in(not_6_out));
  LED Z (.in(or_3_out));
  LED T__LSB (.in(not_7_out));
endmodule
