// Digital circuit counter4test.dig as structural Verilog
module counter4test (
  input  clk,
  input  in_2,
  input  in_3
);

  wire [3:0] upcounter_1_cnt;

  upcounter upcounter_1 (.EN(in_3), .LOAD(in_2), .CLK(clk), .CNT(upcounter_1_cnt));
  Seven_Seg_Hex seven_seg_hex_1 (.d(upcounter_1_cnt), .dp(1'b0));
endmodule
