// Digital circuit upcounter.dig as structural Verilog
module upcounter (
  input  EN,
  input  LOAD,
  input  CLK,
  output [3:0] CNT
);

  wire and_4_out, and_5_out, d_ff_as_1_nq, d_ff_as_2_nq, d_ff_as_3_nq, d_ff_as_4_nq, multiplexer_1_out,
       multiplexer_2_out, multiplexer_3_out, multiplexer_4_out, not_1_out, not_2_out, not_3_out, not_4_out,
       not_5_out, not_6_out;
  wire [0:0] and_1_out, and_2_out;
  wire [1:0] and_3_out;

  or or_1 (and_3_out[1], and_5_out, LOAD, and_4_out);
  and and_1 (and_1_out[0], CNT[0], EN);
  and and_2 (and_2_out[0], CNT[1], and_1_out[0]);
  and and_3 (and_3_out[0], CNT[2], and_2_out[0]);
  Multiplexer #(.Selector_Bits(2)) multiplexer_1 (
    .sel({and_3_out[1], EN}), .in_0(CNT[0]), .in_1(d_ff_as_1_nq), .in_2(1'b1), .in_3(1'b1),
    .out(multiplexer_1_out));
  Multiplexer #(.Selector_Bits(2)) multiplexer_2 (
    .sel({and_3_out[1], and_1_out[0]}), .in_0(CNT[1]), .in_1(d_ff_as_2_nq), .in_2(1'b1), .in_3(1'b1),
    .out(multiplexer_2_out));
  Multiplexer #(.Selector_Bits(2)) multiplexer_3 (
    .sel({and_3_out[1], and_2_out[0]}), .in_0(CNT[2]), .in_1(d_ff_as_3_nq), .in_2(1'b0), .in_3(1'b0),
    .out(multiplexer_3_out));
  Multiplexer #(.Selector_Bits(2)) multiplexer_4 (
    .sel(and_3_out), .in_0(CNT[3]), .in_1(d_ff_as_4_nq), .in_2(1'b0), .in_3(1'b0), .out(multiplexer_4_out));
  D_FF_AS d_ff_as_1 (.Set(1'b0), .D(multiplexer_1_out), .C(CLK), .Clr(1'b0), .Q(CNT[0]), .nQ(d_ff_as_1_nq));
  D_FF_AS d_ff_as_2 (.Set(1'b0), .D(multiplexer_2_out), .C(CLK), .Clr(1'b0), .Q(CNT[1]), .nQ(d_ff_as_2_nq));
  D_FF_AS d_ff_as_3 (.Set(1'b0), .D(multiplexer_3_out), .C(CLK), .Clr(1'b0), .Q(CNT[2]), .nQ(d_ff_as_3_nq));
  D_FF_AS d_ff_as_4 (.Set(1'b0), .D(multiplexer_4_out), .C(CLK), .Clr(1'b0), .Q(CNT[3]), .nQ(d_ff_as_4_nq));
  not not_1 (not_1_out, CNT[3]);
  not not_2 (not_2_out, CNT[2]);
  not not_3 (not_3_out, CNT[1]);
  not not_4 (not_4_out, CNT[0]);
  and and_4 (and_4_out, not_4_out, not_3_out, not_2_out, not_1_out);
  and and_5 (and_5_out, CNT[0], not_5_out, not_6_out, CNT[3]);
  not not_5 (not_5_out, CNT[1]);
  not not_6 (not_6_out, CNT[2]);
endmodule
