// Digital circuit mode_selector.dig as structural Verilog
module mode_selector (
  input  ID,
  input  PWD,
  input  DIS,
  input  RESET,
  input  CLK,
  input  RST,
  output IDO,
  output PWDO
);

  wire and_1_out, and_2_out, and_3_out, jk_ff_1_nq, not_1_out, not_2_out, not_3_out, or_1_out, or_2_out;

  not not_1 (not_1_out, or_1_out);
  not not_2 (not_2_out, RST);
  and and_1 (and_1_out, PWD, not_1_out);
  not not_3 (not_3_out, DIS);
  or or_1 (or_1_out, RESET, not_2_out);
  and and_2 (and_2_out, and_1_out, not_3_out);
  and and_3 (and_3_out, not_3_out, ID);
  or or_2 (or_2_out, and_3_out, or_1_out);
  JK_FF jk_ff_1 (.J(and_2_out), .C(CLK), .K(or_2_out), .Q(PWDO), .nQ(jk_ff_1_nq));
  or or_3 (IDO, jk_ff_1_nq, or_1_out);
endmodule
