// Digital circuit shifter.dig as structural Verilog
module shifter (
  input  [3:0] IN,
  input  EN,
  input  DA,
  input  CLK,
  input  RST,
  output [3:0] ID1,
  output [3:0] ID0,
  output [6:0] HEX
);

  wire and_1_out, not_1_out, or_1_out;
  wire [3:0] multiplexer_1_out, multiplexer_2_out;
  wire [7:0] mul_1_mul;

  and and_1 (and_1_out, EN, DA);
  not not_1 (not_1_out, RST);
  Multiplexer #(.Bits(4)) multiplexer_1 (.sel(not_1_out), .in_0(IN), .in_1(4'b0000), .out(multiplexer_1_out));
  Multiplexer #(.Bits(4)) multiplexer_2 (.sel(not_1_out), .in_0(ID0), .in_1(4'b0000), .out(multiplexer_2_out));
  or or_1 (or_1_out, and_1_out, not_1_out);
  Register #(.Bits(4)) register_1 (.D(multiplexer_1_out), .C(CLK), .en(or_1_out), .Q(ID0));
  Register #(.Bits(4)) register_2 (.D(multiplexer_2_out), .C(CLK), .en(or_1_out), .Q(ID1));
  Mul #(.Bits(4)) mul_1 (.a(ID1), .b(4'b1010), .mul(mul_1_mul));
  Add #(.Bits(7)) add_1 (.a({3'b000, ID0}), .b(mul_1_mul[6:0]), .c_i(1'b0), .s(HEX));  // open: c_o
endmodule
