// Digital circuit shifter_pwd.dig as structural Verilog
module shifter_pwd (
  input  [3:0] DATA_in,
  input  [15:0] PWD_in,
  input  EN,
  input  DA,
  input  CLK,
  input  RST,
  output MATCH,
  output LED1,
  output LED2,
  output LED3,
  output LED4
);

  wire and_1_out, and_2_out, and_3_out, and_4_out, and_5_out, not_1_out, not_2_out, not_3_out, not_4_out,
       not_5_out, not_6_out, not_7_out, or_1_out, or_2_out, or_3_out, or_4_out, or_5_out;
  wire [1:0] add_1_c_o;
  wire [3:0] demultiplexer_1_out_0, demultiplexer_1_out_1, demultiplexer_1_out_2, demultiplexer_1_out_3,
       multiplexer_1_out, multiplexer_2_out, multiplexer_3_out, multiplexer_4_out, register_2_q,
       register_3_q, register_4_q;
  wire [15:0] xnor_1_out;
  wire [15:12] register_1_q;

  and and_1 (and_1_out, DA, EN);
  not not_1 (not_1_out, EN);
  not not_2 (not_2_out, RST);
  or or_1 (or_1_out, not_1_out, not_2_out);
  and and_2 (and_2_out, and_1_out, not_3_out);
  and and_3 (and_3_out, LED1, and_1_out, not_3_out);
  and and_4 (and_4_out, LED2, and_1_out, not_3_out);
  and and_5 (and_5_out, LED3, and_1_out, not_3_out);
  not not_3 (not_3_out, or_1_out);
  JK_FF jk_ff_1 (.J(and_2_out), .C(CLK), .K(or_1_out), .Q(LED1));  // open: nQ
  JK_FF jk_ff_2 (.J(and_3_out), .C(CLK), .K(or_1_out), .Q(LED2));  // open: nQ
  JK_FF jk_ff_3 (.J(and_4_out), .C(CLK), .K(or_1_out), .Q(LED3));  // open: nQ
  JK_FF jk_ff_4 (.J(and_5_out), .C(CLK), .K(or_1_out), .Q(LED4));  // open: nQ
  Add add_1 (.a(LED3), .b(LED2), .c_i(LED1), .s(add_1_c_o[0]), .c_o(add_1_c_o[1]));
  Demultiplexer #(.Bits(4), .Selector_Bits(2)) demultiplexer_1 (
    .sel(add_1_c_o), .in(DATA_in), .out_0(demultiplexer_1_out_0), .out_1(demultiplexer_1_out_1),
    .out_2(demultiplexer_1_out_2), .out_3(demultiplexer_1_out_3));
  not not_4 (not_4_out, LED3);
  not not_5 (not_5_out, LED4);
  not not_6 (not_6_out, LED1);
  not not_7 (not_7_out, LED2);
  Multiplexer #(.Bits(4)) multiplexer_1 (
    .sel(or_1_out), .in_0(demultiplexer_1_out_0), .in_1(4'b0000), .out(multiplexer_1_out));
  Multiplexer #(.Bits(4)) multiplexer_2 (
    .sel(or_1_out), .in_0(demultiplexer_1_out_1), .in_1(4'b0000), .out(multiplexer_2_out));
  Multiplexer #(.Bits(4)) multiplexer_3 (
    .sel(or_1_out), .in_0(demultiplexer_1_out_2), .in_1(4'b0000), .out(multiplexer_3_out));
  Multiplexer #(.Bits(4)) multiplexer_4 (
    .sel(or_1_out), .in_0(demultiplexer_1_out_3), .in_1(4'b0000), .out(multiplexer_4_out));
  or or_2 (or_2_out, not_5_out, or_1_out);
  or or_3 (or_3_out, not_6_out, or_1_out);
  or or_4 (or_4_out, not_7_out, or_1_out);
  or or_5 (or_5_out, not_4_out, or_1_out);
  Register #(.Bits(4)) register_1 (.D(multiplexer_1_out), .C(CLK), .en(or_3_out), .Q(register_1_q));
  Register #(.Bits(4)) register_2 (.D(multiplexer_2_out), .C(CLK), .en(or_4_out), .Q(register_2_q));
  Register #(.Bits(4)) register_3 (.D(multiplexer_3_out), .C(CLK), .en(or_5_out), .Q(register_3_q));
  Register #(.Bits(4)) register_4 (.D(multiplexer_4_out), .C(CLK), .en(or_2_out), .Q(register_4_q));
  assign xnor_1_out = ~({register_1_q, register_2_q, register_3_q, register_4_q} ^ PWD_in);  // XNOr xnor_1, 16 bits wide
  and and_6 (MATCH, xnor_1_out[0], xnor_1_out[1], xnor_1_out[2], xnor_1_out[3], xnor_1_out[4], xnor_1_out[5], xnor_1_out[6], xnor_1_out[7], xnor_1_out[8], xnor_1_out[9], xnor_1_out[10], xnor_1_out[11], xnor_1_out[12], xnor_1_out[13], xnor_1_out[14], xnor_1_out[15]);
endmodule
