// Digital circuit timer.dig as structural Verilog
module timer (
  input  START,
  input  CLK,
  input  RST,
  output RESET,
  output DIS
);

  wire not_1_out, not_2_out, not_3_out, not_4_out, not_5_out, not_6_out, or_1_out;
  wire [8:0] counter_1_out;

  not not_1 (not_1_out, RST);
  or or_1 (or_1_out, not_1_out, RESET);
  Counter #(.Bits(9)) counter_1 (.en(START), .C(CLK), .clr(or_1_out), .out(counter_1_out));  // open: ovf
  not not_2 (not_2_out, counter_1_out[7]);
  not not_3 (not_3_out, counter_1_out[6]);
  not not_4 (not_4_out, counter_1_out[4]);
  not not_5 (not_5_out, counter_1_out[1]);
  not not_6 (not_6_out, counter_1_out[0]);
  and and_1 (RESET, not_2_out, not_3_out, counter_1_out[5], not_4_out, counter_1_out[3], counter_1_out[2], not_5_out, not_6_out, counter_1_out[8]);

  assign DIS = START;
endmodule
