// Digital circuit abs.dig as structural Verilog
module abs (
  input  [3:0] in,
  output sign,
  output [3:0] out
);

  wire [2:0] xor_2_out;

  xor xor_1 (xor_2_out[0], in[0], in[3]);
  xor xor_2 (xor_2_out[1], in[1], in[3]);
  xor xor_3 (xor_2_out[2], in[2], in[3]);
  Add #(.Bits(3)) add_1 (.a(xor_2_out), .b({2'b00, in[3]}), .c_i(1'b0), .s(out[2:0]), .c_o(out[3]));

  assign sign = in[3];
endmodule
