// Digital circuit up-down-tallycounter.dig as structural Verilog
module up_down_tallycounter (
  input  clk,
  input  in_2
);

  wire and_1_out, and_2_out, and_3_out, and_4_out, and_5_out, and_6_out, and_7_out, and_8_out, and_9_out,
       and_10_out, and_11_out, and_12_out, and_13_out, and_14_out, BDOWN_out, BUP_out, cntdecud_1_p1,
       cntdecud_1_p3, cntdecud_1_p8, cntdecud_1_p9, not_1_out, not_2_out, not_3_out, not_4_out, or_1_out,
       or_2_out, or_3_out, or_4_out, or_5_out, Q_0_n_q, Q_1_n_2_q, Q_1_n_q;
  wire [3:0] cntdecud_1_p7, cntdecud_2_p5;

  not not_1 (not_1_out, Q_1_n_q);
  not not_2 (not_2_out, Q_0_n_q);
  and and_1 (and_1_out, BDOWN_out, Q_1_n_q);
  and and_2 (and_2_out, Q_0_n_q, not_1_out);
  and and_3 (and_3_out, BDOWN_out, not_2_out, not_1_out);
  and and_4 (and_4_out, BDOWN_out, Q_0_n_q, Q_1_n_q);
  and and_5 (and_5_out, BDOWN_out, not_1_out);
  and and_6 (and_6_out, Q_0_n_q, not_1_out);
  or or_1 (or_1_out, and_1_out, and_2_out);
  or or_2 (or_2_out, and_3_out, and_4_out);
  or or_3 (or_3_out, and_5_out, and_6_out);
  D_FF Q_1_n (.D(or_1_out), .C(clk), .Q(Q_1_n_q));  // open: nQ
  D_FF Q_0_n (.D(or_2_out), .C(clk), .Q(Q_0_n_q));  // open: nQ
  Button BUP (.out(BUP_out));
  Button BDOWN (.out(BDOWN_out));
  and and_7 (and_7_out, cntdecud_1_p3, cntdecud_1_p9);
  and and_8 (and_8_out, or_3_out, cntdecud_1_p8);
  not not_3 (not_3_out, Q_1_n_2_q);
  not not_4 (not_4_out, cntdecud_1_p1);
  and and_9 (and_9_out, BUP_out, Q_1_n_2_q);
  and and_10 (and_10_out, cntdecud_1_p1, not_3_out);
  and and_11 (and_11_out, BUP_out, not_4_out, not_3_out);
  and and_12 (and_12_out, BUP_out, cntdecud_1_p1, Q_1_n_2_q);
  and and_13 (and_13_out, BUP_out, not_3_out);
  and and_14 (and_14_out, cntdecud_1_p1, not_3_out);
  // cntDECud cntdecud_1: pin names not known; wires that end beside it: cntdecud_1_p1, not_4_out, cntdecud_1_p3, or_3_out, clk, in_2, cntdecud_1_p7, cntdecud_1_p8, cntdecud_1_p9
  // cntDECud cntdecud_2: pin names not known; wires that end beside it: and_7_out, and_8_out, clk, in_2, cntdecud_2_p5
  or or_4 (or_4_out, and_9_out, and_10_out);
  or or_5 (or_5_out, and_11_out, and_12_out);
  or or_6 (cntdecud_1_p3, and_13_out, and_14_out);
  D_FF Q_1_n_2 (.D(or_4_out), .C(clk), .Q(Q_1_n_2_q));  // open: nQ
  D_FF Q_0_n_2 (.D(or_5_out), .C(clk), .Q(cntdecud_1_p1));  // open: nQ
  Seven_Seg_Hex seven_seg_hex_1 (.d(cntdecud_2_p5), .dp(1'b0));
  Seven_Seg_Hex seven_seg_hex_2 (.d(cntdecud_1_p7), .dp(1'b0));

  // Notes on the sheet:
  //   clk: Hz: 10
endmodule
